# Fritzing sketch design (saved by Fritzing 0.9.1b)
breadboards: 1

parts:
  Raspberry_Pi1 = Raspberry Pi B+
  S1 = Pushbutton [package="[THT]"]
  R1 = Resistor [tolerance=±5% resistance=330 package=THT]
  LED1 = LED - 5mm [color="Blue (470nm)" package="5 mm [THT]"]

nets:
  3V3: Raspberry_Pi1.3v3, Raspberry_Pi1.3V3, S1.Pin_3, S1.Pin_4
  N1: Raspberry_Pi1.GPIO17, S1.Pin_1, S1.Pin_2, R1.Pin_0
  N2: Raspberry_Pi1.GPIO18, LED1.cathode
  N3: Raspberry_Pi1.GND, R1.Pin_1, LED1.anode

notes:
  Inspired by:
  https://learn.adafruit.com/node-embedded-development/events
